# Fritzing sketch I2C-sensor (saved by Fritzing 0.9.3b)
breadboards: 1

parts:
  Part1 = Arduino Uno (Rev3)
  GY1 = MPU-6050 Board GY-521 [form="♀ (female)" package=THT]

nets:
  N1: Part1.A4/SDA, GY1.pin4
  N2: Part1.A5/SCL, GY1.pin3
  N3: Part1.5V, GY1.pin1
  N4: Part1.GND, GY1.pin2

notes:
  SCL
  SDA

custom parts:
  MPU-6050 Board GY-521: Acelerometro y Giroscopio MPU-6050 Board GY-521
