# Fritzing sketch run-motor (saved by Fritzing 0.9.3b)
breadboards: 1

parts:
  Part1 = Arduino Uno (Rev3)
  Q1 = Basic FET N-Channel [package="TO220 [THT]"]
  U1 = Vibration Motor- ROB-08449 [package=vibe-motor-10mm]
  V1 = DC Power [voltage=2.5V]

nets (from the schematic view):
  N1: Part1.D9_PWM, Q1.gate
  N2: Part1.GND, Q1.source, V1.V-
  N3: Q1.drain, U1.-
  N4: U1.+, V1.V+

notes:
  2.5V Power supply in
