# Fritzing sketch sensor-driven-led (saved by Fritzing 0.9.3b)
breadboards: 1

parts:
  Part1 = Arduino Uno (Rev3)
  R1 = Resistor [tolerance=±5% resistance=220 package=THT]
  R2 = Resistor [tolerance=±5% resistance=220 package=THT]
  LED1 = LED - 5mm [color="Green (555nm)" package="5 mm [THT]"]
  LED2 = LED - 5mm [color="Yellow (595nm)" package="5 mm [THT]"]
  R3 = Resistor [tolerance=±5% resistance=5.6k package=THT]
  R4 = Photocell (LDR) [package=THT]

nets:
  N1: Part1.A0, R3.Pin_0, R4.pin_0
  GND: Part1.GND, LED1.cathode, LED2.cathode, R4.pin_1
  N2: Part1.D5_PWM, R2.Pin_0
  N3: Part1.D6_PWM, R1.Pin_0
  N4: Part1.5V, R3.Pin_1
  N5: R1.Pin_1, LED1.anode
  N6: R2.Pin_1, LED2.anode
