# Fritzing sketch sensor-driven-servo (saved by Fritzing 0.9.3b)
breadboards: 1

parts:
  Part1 = Arduino Uno (Rev3)
  J1 = Basic Servo
  R1 = TRIMPOT [package=trimpot_pth_s3_lock]

nets:
  N1: Part1.A0, R1.WIPER
  N2: Part1.D9_PWM, J1.pulse
  5V: Part1.5V, J1.vcc, R1.CCW
  GND: Part1.GND, J1.gnd, R1.CW
