# Fritzing sketch voltage-regulation (saved by Fritzing 0.9.3b)
breadboards: 1

parts:
  V1 = DC Power [voltage=5]  # not connected
  V2 = DC Power [voltage=5]  # not connected
  U1 = Voltage Regulator - 5V [part_number=7805 package="TO220 [THT]"]
  C1 = Electrolytic Capacitor [capacitance=10µF package="100 mil [THT, electrolytic]"]
  C2 = Electrolytic Capacitor [capacitance=10µF package="100 mil [THT, electrolytic]"]
  R1 = Resistor [tolerance=±5% resistance=100 package=THT]
  R2 = Resistor [tolerance=±5% resistance=100 package=THT]

nets:
  N1: U1.input_voltage, C2.+
  N2: U1.GND, C1.-, C2.-, R1.Pin_1, R2.Pin_1
  N3: U1.output_voltage, C1.+, R1.Pin_0, R2.Pin_0

notes:
  9V
  Touch to VOUT
  Touch to ground
  5V
  Load resistors for testing loaded output
