# Fritzing sketch multichannel-driver (saved by Fritzing 0.9.3b)
breadboards: 1

parts:
  M3 = DC Motor
  M4 = DC Motor
  V1 = DC Power [voltage=3V]
  IC2 = ULN2003A [package="DIP16 [THT]"]

nets:
  N1: M3.pin_1, M4.pin_1, V1.V+, IC2.COM_-_Common
  N2: M3.pin_2, IC2.Out_7
  N3: M4.pin_2, IC2.Out_6
  N4: V1.V-, IC2.0V

notes:
  5V here to turn on motor
  Gnd of 5V supply
  3V
