# Fritzing sketch power-switch (saved by Fritzing 0.9.2b)
breadboards: 1

parts:
  U1 = SWITCH_SPDT [package=kps-1290]
  R1 = Resistor [tolerance=±5% resistance=220 package=THT]
  LED1 = LED - 5mm [color="Red (633nm)" package="5 mm [THT]"]

nets:
  N1: U1.O, R1.Pin_1
  N2: R1.Pin_0, LED1.anode

notes:
  5V
  0.19A
