# Fritzing sketch transistor-and-sensor-for-power (saved by Fritzing 0.9.3b)
breadboards: 1

parts:
  R1 = PHOTOCELL [package=photocell-kit]
  M1 = DC Motor
  V1 = DC Power [voltage=5V]
  V2 = DC Power [voltage=2V]
  Q3 = Basic FET N-Channel [package="TO220 [THT]"]
  R2 = Resistor [tolerance=±5% resistance=5.6k package=THT]
  R3 = Resistor [tolerance=±5% resistance=5.6k package=THT]

nets:
  N1: R1.P$1, V1.V-, V2.V-, Q3.source
  N2: R1.P$2, Q3.gate, R2.Pin_1, R3.Pin_1
  N3: M1.pin_1, V2.V+
  N4: M1.pin_2, Q3.drain
  N5: V1.V+, R2.Pin_0, R3.Pin_0

notes:
  2V
  .17A
  5.0V
  .01A
  IRF540N
