# Fritzing sketch voltage-divider (saved by Fritzing 0.9.3b)
breadboards: 1

parts:
  R1 = Resistor [package="2010 [SMD]"]
  R2 = Resistor [package="2010 [SMD]"]

nets:
  N1: R1.Pin_0, R2.Pin_1

notes:
  2.5V
  5V
  .1A
