# Fritzing sketch Chip-blink (saved by Fritzing 0.9.3b)

parts:
  C_H_I_P_1 = Next Thing Co. C.H.I.P
  LED1 = LED - 5mm [color="Red (633nm)" package="5 mm [THT]"]

nets:
  N1: C_H_I_P_1.CSID6, LED1.anode
  N2: C_H_I_P_1.GND, LED1.cathode
