# Fritzing sketch NodeMCU-I2C-ADC (saved by Fritzing 0.9.3b)
breadboards: 1

parts:
  Part1 = Adafruit ADS1015 12Bit I2C ADC [part_number="Adafruit #1083"]
  U1 = NodeMCU V1.0
  R1 = TRIMPOT [package=3362u-2]

nets:
  N1: Part1.AIN0, R1.WIPER
  GND: Part1.ADDR, Part1.GND, U1.GND, R1.CW
  N2: Part1.SDA, U1.D2
  N3: Part1.SCL, U1.D1
  VDD: Part1.VDD, U1.3V3, R1.CCW

custom parts:
  Adafruit ADS1015 12Bit I2C ADC: For microcontrollers without an analog-to-digital converter or when you want a higher-precision ADC, the ADS1015 provides 12-bit precision at 3300 samples/second over I2C. The chip can be configured as 4 single-ended input channels, or two differential channels. As a nice bonus, it even includes a programmable gain amplifier, up to x16, to help boost up smaller single/differential signals to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
  NodeMCU V1.0: ESP8266 based NodeMCU
