# Fritzing sketch NodeMCU-send-OSC (saved by Fritzing 0.9.3b)
breadboards: 1

parts:
  U1 = NodeMCU V1.0
  R1 = Resistor [tolerance=±5% resistance=10k package=THT]
  S1 = Pushbutton [package="[THT]"]

nets:
  N1: U1.D0, R1.Pin_0, S1.Pin_3, S1.Pin_4
  N2: U1.3V3, S1.Pin_1, S1.Pin_2
  N3: U1.GND, R1.Pin_1

custom parts:
  NodeMCU V1.0: ESP8266 based NodeMCU
